# Fritzing sketch InvertedPendulum (saved by Fritzing 1.0.6)

parts:
  U1 = ESP32-38PinWide [part_number=ESP32-38PinWide]
  Bauteil1 = 9-DOF Absolute Orientation IMU Fusion Breakout - BNO055
  M2 = DC Motor [voltage_(max)=6V voltage_(min)=3V]
  A1 = L298N DC motor driver
  M3 = DC Motor [voltage_(max)=6V voltage_(min)=3V]
  Power_plug1 = Power plug

nets:
  N1: U1.3.3, Bauteil1.3.3V
  N2: U1.GPIO33, A1.ENB
  N3: U1.GPIO16, A1.IN1
  N4: U1.GPIO17, A1.IN2
  N5: U1.GPIO18, A1.IN3
  N6: U1.GPIO19, A1.IN4
  N7: U1.GPIO21, Bauteil1.SDA_5V
  N8: U1.GPIO22, Bauteil1.SCL_5V
  N9: U1.GPIO23, A1.ENA
  GND: U1.GND, Bauteil1.GND, Bauteil1.I2CADDR_3V, A1.GND, Power_plug1.GND
  N10: M2.pin_1, A1.OUT2
  N11: M2.pin_2, A1.OUT1
  12V: A1.12V, A1.5V-ENA-JMP-I, A1.5V-ENA-JMP-O, Power_plug1.VCC
  N12: A1.OUT3, M3.pin_2
  N13: A1.OUT4, M3.pin_1

custom parts:
  ESP32-38PinWide: Generic 38-Pin ESP32 with wide format (only access to one side of pins on a breadboard) based on Stephen Lilley's HiLetgo ESP-WROOM-32 ESP32 ESP-32S Development Board.
  9-DOF Absolute Orientation IMU Fusion Breakout - BNO055: A MEMS accelerometer, magnetometer and gyroscope on a single die with a high speed ARM Cortex-M0 based processor to digest all the sensor data, abstract the sensor fusion and real time requirements away, and spit out data you can use in quaternions, Euler angles or vectors.
  L298N DC motor driver: This L298N Motor Driver Module is a high power motor driver module for driving DC and Stepper Motors. This module consists of an L298 motor driver IC and a 78M05 5V regulator.
